// Logisim project main.circ as structural Verilog: 8 circuits, main circuit main
module main (
);

  wire and_1_out, button_1_out, button_2_trigger, button_3_out, button_5_out, button_7_out, button_9_out,
       button_11_out, button_13_out, cdm_8_1_p2, cdm_8_1_p4, cdm_8_1_p5, cdm_8_1_p6, cdm_8_1_p7, cdm_8_1_p8,
       cdm_8_1_p9, cdm_8_1_p10, Cl, code, data, display_driver_2_clk_2, display_driver_2_dir_2,
       display_driver_2_isempty, display_driver_3_clk_2, display_driver_3_dir_2, display_driver_4_clk_2,
       display_driver_4_dir_2, display_driver_5_clk_2, display_driver_5_dir_2, display_driver_6_clk_2,
       display_driver_6_dir_2, display_driver_7_clk_2, display_driver_7_dir_2, display_driver_8_clk_2,
       display_driver_8_dir_2, display_driver_9_clk_2, display_driver_9_dir_2, display_driver_10_clk_2,
       display_driver_10_dir_2, display_driver_11_clk_2, display_driver_11_dir_2, display_driver_12_clk_2,
       display_driver_12_dir_2, display_driver_13_clk_2, display_driver_13_dir_2, display_driver_14_clk_2,
       display_driver_14_dir_2, I_Osel, in_out, nand_1_out, not_1_out, not_2_out, pull_resistor_1_node, RAM;
  wire [3:0] button_2_addr_2, button_4_addr_2, button_6_addr_2, button_8_addr_2, button_10_addr_2,
       button_12_addr_2, display_driver_1_out_6, display_driver_1_out_7, display_driver_2_addr_2,
       display_driver_2_out_6, display_driver_2_out_7, display_driver_2_pos_2, display_driver_3_addr_2,
       display_driver_3_out_6, display_driver_3_out_7, display_driver_3_pos_2, display_driver_4_addr_2,
       display_driver_4_out_6, display_driver_4_out_7, display_driver_4_pos_2, display_driver_4_pos_3,
       display_driver_5_addr_2, display_driver_5_out_6, display_driver_5_out_7, display_driver_5_pos_2,
       display_driver_6_addr_2, display_driver_6_out_6, display_driver_6_out_7, display_driver_6_pos_2,
       display_driver_6_pos_3, display_driver_7_addr_2, display_driver_7_out_6, display_driver_7_out_7,
       display_driver_7_pos_2, display_driver_8_addr_2, display_driver_8_out_6, display_driver_8_out_7,
       display_driver_8_pos_2, display_driver_8_pos_3, display_driver_9_addr_2, display_driver_9_out_6,
       display_driver_9_out_7, display_driver_9_pos_2, display_driver_9_pos_3, display_driver_10_addr_2,
       display_driver_10_out_6, display_driver_10_out_7, display_driver_10_pos_2, display_driver_11_addr_2,
       display_driver_11_out_6, display_driver_11_out_7, display_driver_11_pos_2, display_driver_11_pos_3,
       display_driver_12_addr_2, display_driver_12_out_6, display_driver_12_out_7, display_driver_12_pos_2,
       display_driver_13_addr_2, display_driver_13_out_6, display_driver_13_out_7, display_driver_13_pos_2,
       display_driver_13_pos_3, display_driver_14_addr_2, display_driver_14_out_6, display_driver_14_out_7,
       I_Oaddr, inc4_1_out, pos;
  wire [7:0] adder_2_out, adder_3_out, adder_4_out, adder_5_out, adder_6_out, adder_7_out, adder_8_out,
       adder_9_out, adder_10_out, adder_11_out, adder_12_out, adder_13_out, adder_14_out, botScore,
       cdm_8_1_p13, display_driver_1_register, display_driver_2_data_2, display_driver_2_register,
       display_driver_3_data_2, display_driver_3_register, display_driver_4_data_2,
       display_driver_4_register, display_driver_5_data_2, display_driver_5_register,
       display_driver_6_data_2, display_driver_6_register, display_driver_7_data_2,
       display_driver_7_register, display_driver_8_data_2, display_driver_8_register,
       display_driver_9_data_2, display_driver_9_register, display_driver_10_data_2,
       display_driver_10_register, display_driver_11_data_2, display_driver_11_register,
       display_driver_12_data_2, display_driver_12_register, display_driver_13_data_2,
       display_driver_13_register, display_driver_14_data_2, display_driver_14_register, I_Odat, I_Odat_in;
  wire [7:4] cdm_8_1_p12;

  Display_Driver display_driver_1 (
    .data(display_driver_2_data_2), .pos(display_driver_2_pos_2), .addr(display_driver_2_addr_2),
    .clk(display_driver_2_clk_2), .dir(display_driver_2_dir_2), .out_6(display_driver_1_out_6),
    .out_7(display_driver_1_out_7), .register(display_driver_1_register), .data_2(I_Odat_in));  // open: pos_2, addr_2, clk_2, dir_2, pos_3, isEmpty
  adder adder_1 (.in1(adder_2_out), .in2(display_driver_1_register), .out(botScore));
  Hex_Digit_Display hex_digit_display_1 (.value(display_driver_1_out_7), .dp(1'b0));
  Hex_Digit_Display hex_digit_display_2 (.value(display_driver_1_out_6), .dp(1'b0));
  // Probe on button_2_addr_2
  and and_1 (and_1_out, Cl, I_Osel);
  Display_Driver display_driver_2 (
    .data(display_driver_3_data_2), .pos(display_driver_3_pos_2), .addr(display_driver_3_addr_2),
    .clk(display_driver_3_clk_2), .dir(display_driver_3_dir_2), .out_6(display_driver_2_out_6),
    .out_7(display_driver_2_out_7), .register(display_driver_2_register), .data_2(display_driver_2_data_2),
    .pos_2(display_driver_2_pos_2), .addr_2(display_driver_2_addr_2), .clk_2(display_driver_2_clk_2),
    .dir_2(display_driver_2_dir_2), .isEmpty(display_driver_2_isempty));  // open: pos_3
  adder adder_2 (.in1(adder_5_out), .in2(display_driver_2_register), .out(adder_2_out));
  Hex_Digit_Display hex_digit_display_3 (.value(display_driver_2_out_6), .dp(1'b0));
  Hex_Digit_Display hex_digit_display_4 (.value(display_driver_2_out_7), .dp(1'b0));
  Hex_Digit_Display hex_digit_display_5 (.value(display_driver_4_out_6), .dp(1'b0));
  Hex_Digit_Display hex_digit_display_6 (.value(display_driver_4_out_7), .dp(1'b0));
  Pull_Resistor pull_resistor_1 (.node(pull_resistor_1_node));
  adder adder_3 (.in1({8{1'b0}}), .in2(display_driver_4_register), .out(adder_3_out));
  Button button_1 (.out(button_1_out));
  Display_Driver display_driver_3 (
    .data(display_driver_5_data_2), .pos(display_driver_5_pos_2), .addr(display_driver_5_addr_2),
    .clk(display_driver_5_clk_2), .dir(display_driver_5_dir_2), .out_6(display_driver_3_out_6),
    .out_7(display_driver_3_out_7), .register(display_driver_3_register), .data_2(display_driver_3_data_2),
    .pos_2(display_driver_3_pos_2), .addr_2(display_driver_3_addr_2), .clk_2(display_driver_3_clk_2),
    .dir_2(display_driver_3_dir_2), .isEmpty(display_driver_2_isempty));  // open: pos_3
  Hex_Digit_Display hex_digit_display_7 (.value(display_driver_3_out_6), .dp(1'b0));
  Hex_Digit_Display hex_digit_display_8 (.value(display_driver_6_out_6), .dp(1'b0));
  adder adder_4 (.in1(adder_3_out), .in2(display_driver_6_register), .out(adder_4_out));
  Display_Driver display_driver_4 (
    .data(I_Odat), .pos(4'b0001), .addr(I_Oaddr), .clk(and_1_out), .dir(in_out),
    .out_6(display_driver_4_out_6), .out_7(display_driver_4_out_7), .register(display_driver_4_register),
    .data_2(display_driver_4_data_2), .pos_2(display_driver_4_pos_2), .addr_2(display_driver_4_addr_2),
    .clk_2(display_driver_4_clk_2), .dir_2(display_driver_4_dir_2), .pos_3(display_driver_4_pos_3),
    .isEmpty(pull_resistor_1_node));
  button button_2 (
    .addr_2(button_2_addr_2), .addr(button_4_addr_2), .pos(display_driver_4_pos_3), .button(button_1_out),
    .trigger(button_2_trigger));
  Button button_3 (.out(button_3_out));
  Clock clock_1 (.out(Cl));
  and and_2 (I_Osel, not_1_out, Cl, data);
  Display_Driver display_driver_5 (
    .data(display_driver_7_data_2), .pos(display_driver_7_pos_2), .addr(display_driver_7_addr_2),
    .clk(display_driver_7_clk_2), .dir(display_driver_7_dir_2), .out_6(display_driver_5_out_6),
    .out_7(display_driver_5_out_7), .register(display_driver_5_register), .data_2(display_driver_5_data_2),
    .pos_2(display_driver_5_pos_2), .addr_2(display_driver_5_addr_2), .clk_2(display_driver_5_clk_2),
    .dir_2(display_driver_5_dir_2), .isEmpty(display_driver_2_isempty));  // open: pos_3
  adder adder_5 (.in1(adder_7_out), .in2(display_driver_3_register), .out(adder_5_out));
  Hex_Digit_Display hex_digit_display_9 (.value(display_driver_3_out_7), .dp(1'b0));
  Hex_Digit_Display hex_digit_display_10 (.value(display_driver_5_out_6), .dp(1'b0));
  Hex_Digit_Display hex_digit_display_11 (.value(display_driver_6_out_7), .dp(1'b0));
  Hex_Digit_Display hex_digit_display_12 (.value(display_driver_8_out_6), .dp(1'b0));
  adder adder_6 (.in1(adder_4_out), .in2(display_driver_8_register), .out(adder_6_out));
  Display_Driver display_driver_6 (
    .data(display_driver_4_data_2), .pos(display_driver_4_pos_2), .addr(display_driver_4_addr_2),
    .clk(display_driver_4_clk_2), .dir(display_driver_4_dir_2), .out_6(display_driver_6_out_6),
    .out_7(display_driver_6_out_7), .register(display_driver_6_register), .data_2(display_driver_6_data_2),
    .pos_2(display_driver_6_pos_2), .addr_2(display_driver_6_addr_2), .clk_2(display_driver_6_clk_2),
    .dir_2(display_driver_6_dir_2), .pos_3(display_driver_6_pos_3), .isEmpty(pull_resistor_1_node));
  button button_4 (
    .addr_2(button_4_addr_2), .addr(button_6_addr_2), .pos(display_driver_6_pos_3), .button(button_3_out),
    .trigger(button_2_trigger));
  // Probe on cdm_8_1_p4
  // Probe on cdm_8_1_p6
  // Probe on cdm_8_1_p5
  // Probe on cdm_8_1_p2
  Button button_5 (.out(button_5_out));
  not not_1 (not_1_out, nand_1_out);
  and and_3 (RAM, nand_1_out, data);
  Display_Driver display_driver_7 (
    .data(display_driver_10_data_2), .pos(display_driver_10_pos_2), .addr(display_driver_10_addr_2),
    .clk(display_driver_10_clk_2), .dir(display_driver_10_dir_2), .out_6(display_driver_7_out_6),
    .out_7(display_driver_7_out_7), .register(display_driver_7_register), .data_2(display_driver_7_data_2),
    .pos_2(display_driver_7_pos_2), .addr_2(display_driver_7_addr_2), .clk_2(display_driver_7_clk_2),
    .dir_2(display_driver_7_dir_2), .isEmpty(display_driver_2_isempty));  // open: pos_3
  adder adder_7 (.in1(adder_8_out), .in2(display_driver_5_register), .out(adder_7_out));
  Hex_Digit_Display hex_digit_display_13 (.value(display_driver_7_out_6), .dp(1'b0));
  Hex_Digit_Display hex_digit_display_14 (.value(display_driver_5_out_7), .dp(1'b0));
  Hex_Digit_Display hex_digit_display_15 (.value(display_driver_8_out_7), .dp(1'b0));
  Hex_Digit_Display hex_digit_display_16 (.value(display_driver_9_out_6), .dp(1'b0));
  Display_Driver display_driver_8 (
    .data(display_driver_6_data_2), .pos(display_driver_6_pos_2), .addr(display_driver_6_addr_2),
    .clk(display_driver_6_clk_2), .dir(display_driver_6_dir_2), .out_6(display_driver_8_out_6),
    .out_7(display_driver_8_out_7), .register(display_driver_8_register), .data_2(display_driver_8_data_2),
    .pos_2(display_driver_8_pos_2), .addr_2(display_driver_8_addr_2), .clk_2(display_driver_8_clk_2),
    .dir_2(display_driver_8_dir_2), .pos_3(display_driver_8_pos_3), .isEmpty(pull_resistor_1_node));
  button button_6 (
    .addr_2(button_6_addr_2), .addr(button_8_addr_2), .pos(display_driver_8_pos_3), .button(button_7_out),
    .trigger(button_2_trigger));
  Button button_7 (.out(button_7_out));
  // Probe on cdm_8_1_p7
  // Probe on cdm_8_1_p8
  // Probe on cdm_8_1_p9
  nand nand_1 (nand_1_out, cdm_8_1_p12[4], cdm_8_1_p12[5], cdm_8_1_p12[6], cdm_8_1_p12[7]);
  adder adder_8 (.in1(adder_10_out), .in2(display_driver_7_register), .out(adder_8_out));
  Hex_Digit_Display hex_digit_display_17 (.value(display_driver_10_out_6), .dp(1'b0));
  Hex_Digit_Display hex_digit_display_18 (.value(display_driver_7_out_7), .dp(1'b0));
  Hex_Digit_Display hex_digit_display_19 (.value(display_driver_9_out_7), .dp(1'b0));
  Hex_Digit_Display hex_digit_display_20 (.value(display_driver_11_out_6), .dp(1'b0));
  adder adder_9 (.in1(adder_6_out), .in2(display_driver_9_register), .out(adder_9_out));
  Display_Driver display_driver_9 (
    .data(display_driver_8_data_2), .pos(display_driver_8_pos_2), .addr(display_driver_8_addr_2),
    .clk(display_driver_8_clk_2), .dir(display_driver_8_dir_2), .out_6(display_driver_9_out_6),
    .out_7(display_driver_9_out_7), .register(display_driver_9_register), .data_2(display_driver_9_data_2),
    .pos_2(display_driver_9_pos_2), .addr_2(display_driver_9_addr_2), .clk_2(display_driver_9_clk_2),
    .dir_2(display_driver_9_dir_2), .pos_3(display_driver_9_pos_3), .isEmpty(pull_resistor_1_node));
  button button_8 (
    .addr_2(button_8_addr_2), .addr(button_10_addr_2), .pos(display_driver_9_pos_3), .button(button_9_out),
    .trigger(button_2_trigger));
  Button button_9 (.out(button_9_out));
  // CdM_8 cdm_8_1: pin names not known; wires that end beside it: Cl, cdm_8_1_p2, button_5_out, cdm_8_1_p4, cdm_8_1_p5, cdm_8_1_p6, cdm_8_1_p7, cdm_8_1_p8, cdm_8_1_p9, cdm_8_1_p10, in_out, {cdm_8_1_p12, I_Oaddr}, cdm_8_1_p13
  Display_Driver display_driver_10 (
    .data(display_driver_12_data_2), .pos(display_driver_12_pos_2), .addr(display_driver_12_addr_2),
    .clk(display_driver_12_clk_2), .dir(display_driver_12_dir_2), .out_6(display_driver_10_out_6),
    .out_7(display_driver_10_out_7), .register(display_driver_10_register),
    .data_2(display_driver_10_data_2), .pos_2(display_driver_10_pos_2), .addr_2(display_driver_10_addr_2),
    .clk_2(display_driver_10_clk_2), .dir_2(display_driver_10_dir_2), .isEmpty(display_driver_2_isempty));  // open: pos_3
  adder adder_10 (.in1(adder_12_out), .in2(display_driver_10_register), .out(adder_10_out));
  Hex_Digit_Display hex_digit_display_21 (.value(display_driver_10_out_7), .dp(1'b0));
  Hex_Digit_Display hex_digit_display_22 (.value(display_driver_11_out_7), .dp(1'b0));
  adder adder_11 (.in1(adder_9_out), .in2(display_driver_11_register), .out(adder_11_out));
  Display_Driver display_driver_11 (
    .data(display_driver_9_data_2), .pos(display_driver_9_pos_2), .addr(display_driver_9_addr_2),
    .clk(display_driver_9_clk_2), .dir(display_driver_9_dir_2), .out_6(display_driver_11_out_6),
    .out_7(display_driver_11_out_7), .register(display_driver_11_register),
    .data_2(display_driver_11_data_2), .pos_2(display_driver_11_pos_2), .addr_2(display_driver_11_addr_2),
    .clk_2(display_driver_11_clk_2), .dir_2(display_driver_11_dir_2), .pos_3(display_driver_11_pos_3),
    .isEmpty(pull_resistor_1_node));
  button button_10 (
    .addr_2(button_10_addr_2), .addr(button_12_addr_2), .pos(display_driver_11_pos_3),
    .button(button_11_out), .trigger(button_2_trigger));
  Button button_11 (.out(button_11_out));
  assign I_Odat = not_2_out ? cdm_8_1_p13 : 8'bz;  // Controlled_Buffer controlled_buffer_1
  not not_2 (not_2_out, in_out);
  assign cdm_8_1_p13 = in_out ? I_Odat : 8'bz;  // Controlled_Buffer controlled_buffer_2
  Display_Driver display_driver_12 (
    .data(display_driver_14_data_2), .pos(inc4_1_out), .addr(display_driver_14_addr_2),
    .clk(display_driver_14_clk_2), .dir(display_driver_14_dir_2), .out_6(display_driver_12_out_6),
    .out_7(display_driver_12_out_7), .register(display_driver_12_register),
    .data_2(display_driver_12_data_2), .pos_2(display_driver_12_pos_2), .addr_2(display_driver_12_addr_2),
    .clk_2(display_driver_12_clk_2), .dir_2(display_driver_12_dir_2), .isEmpty(display_driver_2_isempty));  // open: pos_3
  adder adder_12 (.in1({8{1'b0}}), .in2(display_driver_12_register), .out(adder_12_out));
  Hex_Digit_Display hex_digit_display_23 (.value(display_driver_12_out_6), .dp(1'b0));
  Hex_Digit_Display hex_digit_display_24 (.value(display_driver_12_out_7), .dp(1'b0));
  Hex_Digit_Display hex_digit_display_25 (.value(display_driver_13_out_7), .dp(1'b0));
  Hex_Digit_Display hex_digit_display_26 (.value(display_driver_13_out_6), .dp(1'b0));
  adder adder_13 (.in1(adder_11_out), .in2(display_driver_13_register), .out(adder_13_out));
  Display_Driver display_driver_13 (
    .data(display_driver_11_data_2), .pos(display_driver_11_pos_2), .addr(display_driver_11_addr_2),
    .clk(display_driver_11_clk_2), .dir(display_driver_11_dir_2), .out_6(display_driver_13_out_6),
    .out_7(display_driver_13_out_7), .register(display_driver_13_register),
    .data_2(display_driver_13_data_2), .pos_2(display_driver_13_pos_2), .addr_2(display_driver_13_addr_2),
    .clk_2(display_driver_13_clk_2), .dir_2(display_driver_13_dir_2), .pos_3(display_driver_13_pos_3),
    .isEmpty(pull_resistor_1_node));
  button button_12 (
    .addr_2(button_12_addr_2), .pos(display_driver_13_pos_3), .button(button_13_out),
    .trigger(button_2_trigger));  // open: addr
  Button button_13 (.out(button_13_out));
  Decoder #(.enable("false")) decoder_1 (.out0(code), .out1(data), .sel(cdm_8_1_p10));
  inc4 inc4_1 (.in(pos), .out(inc4_1_out));
  Pull_Resistor pull_resistor_2 (.node(display_driver_2_isempty));
  Hex_Digit_Display hex_digit_display_27 (.value(display_driver_14_out_7));  // open: dp
  Hex_Digit_Display hex_digit_display_28 (.value(display_driver_14_out_6));  // open: dp
  adder adder_14 (.in1(adder_13_out), .in2(display_driver_14_register), .out(adder_14_out));
  Pull_Resistor pull_resistor_3 (.node({cdm_8_1_p12, I_Oaddr}));
  WLD wld_1 (
    .p1(botScore), .end1(display_driver_2_isempty), .end2(pull_resistor_1_node), .p2(adder_14_out));  // open: p1win, p2win, GameOver
  Display_Driver display_driver_14 (
    .data(display_driver_13_data_2), .pos(display_driver_13_pos_2), .addr(display_driver_13_addr_2),
    .clk(display_driver_13_clk_2), .dir(display_driver_13_dir_2), .out_6(display_driver_14_out_6),
    .out_7(display_driver_14_out_7), .register(display_driver_14_register),
    .data_2(display_driver_14_data_2), .pos_2(pos), .addr_2(display_driver_14_addr_2),
    .clk_2(display_driver_14_clk_2), .dir_2(display_driver_14_dir_2));  // open: pos_3, isEmpty
  RAM ram_1 (.addr({cdm_8_1_p12, I_Oaddr}), .data(I_Odat), .sel(code));  // open: clk, ld, clr
  RAM ram_2 (.addr({cdm_8_1_p12, I_Oaddr}), .data(I_Odat), .sel(RAM));  // open: clk, ld, clr

  // Other names for the same wires on the sheet: rd_wr = in_out
endmodule

module adder (
  input  [7:0] in1,
  input  [7:0] in2,
  output [7:0] out
);

  Adder adder_1 (.a(in1), .b(in2), .out(out), .cin(1'b0));  // open: cout
endmodule

module WLD (
  input  [7:0] p1,
  input  end1,
  input  end2,
  input  [7:0] p2,
  output p1win,
  output p2win,
  output GameOver
);

  wire comparator_1_eq, comparator_1_gt, comparator_1_lt, or_1_out, or_2_out;

  nand nand_1 (GameOver, end1, end2);
  Comparator comparator_1 (.a(p1), .b(p2), .gt(comparator_1_gt), .eq(comparator_1_eq), .lt(comparator_1_lt));
  and and_1 (p1win, or_1_out, GameOver);
  or or_1 (or_1_out, comparator_1_gt, comparator_1_eq);
  or or_2 (or_2_out, comparator_1_eq, comparator_1_lt);
  and and_2 (p2win, or_2_out, GameOver);

  // Other names for the same wires on the sheet: over = GameOver
endmodule

module button (
  input  [3:0] pos,
  input  [3:0] addr,
  input  button,
  output [3:0] addr_2,
  output trigger
);

  assign addr = button ? pos : 4'bz;  // Controlled_Buffer controlled_buffer_1
  Transistor #(.\type ("n")) transistor_1 (.in(1'b0), .out(trigger), .gate(button));

  assign addr_2 = addr;
endmodule

module inc4 (
  input  [3:0] in,
  output [3:0] out
);

  Adder #(.width(4)) adder_1 (.a(in), .b(4'b0001), .out(out), .cin(1'b0));  // open: cout
endmodule

module Add_3_Module (
  input  in_1,
  input  in_2,
  input  in_3,
  input  in_4,
  output out_5,
  output out_6,
  output out_7,
  output out_8
);

  wire comparator_1_lt;
  wire [3:0] adder_1_out;

  Adder #(.width(4)) adder_1 (.a(4'b0011), .b({in_1, in_2, in_3, in_4}), .out(adder_1_out));  // open: cin, cout
  Comparator #(.width(4), .mode("unsigned")) comparator_1 (
    .a(4'b0100), .b({in_1, in_2, in_3, in_4}), .lt(comparator_1_lt));  // open: gt, eq
  Transistor #(.\type ("n"), .gate("br"), .width(4)) transistor_1 (
    .in(adder_1_out), .out({out_5, out_6, out_7, out_8}), .gate(comparator_1_lt));
  Transistor #(.width(4)) transistor_2 (
    .in({in_1, in_2, in_3, in_4}), .out({out_5, out_6, out_7, out_8}), .gate(comparator_1_lt));
endmodule

module BCD_Converter (
  input  [7:0] in_1,
  output [3:0] out_2,
  output [3:0] out_3
);

  wire add_3_module_2_out_6, add_3_module_2_out_7, add_3_module_2_out_8, add_3_module_3_out_5,
       add_3_module_3_out_6, add_3_module_3_out_7, add_3_module_3_out_8, add_3_module_4_out_5,
       add_3_module_4_out_6, add_3_module_4_out_7, add_3_module_4_out_8, add_3_module_5_out_5,
       add_3_module_5_out_6, add_3_module_5_out_7, add_3_module_5_out_8, add_3_module_6_out_5,
       add_3_module_6_out_6, add_3_module_6_out_7, add_3_module_6_out_8;

  Add_3_Module add_3_module_1 (
    .out_6(out_2[3]), .out_7(out_2[2]), .out_8(out_2[1]), .in_1(add_3_module_2_out_6),
    .in_2(add_3_module_2_out_7), .in_3(add_3_module_2_out_8), .in_4(add_3_module_3_out_5));  // open: out_5
  Add_3_Module add_3_module_2 (
    .out_6(add_3_module_2_out_6), .out_7(add_3_module_2_out_7), .out_8(add_3_module_2_out_8), .in_1(1'b0),
    .in_2(add_3_module_6_out_5), .in_3(add_3_module_5_out_5), .in_4(add_3_module_4_out_5));  // open: out_5
  Add_3_Module add_3_module_3 (
    .out_5(add_3_module_3_out_5), .out_6(add_3_module_3_out_6), .out_7(add_3_module_3_out_7),
    .out_8(add_3_module_3_out_8), .in_1(add_3_module_4_out_6), .in_2(add_3_module_4_out_7),
    .in_3(add_3_module_4_out_8), .in_4(in_1[2]));
  Add_3_Module add_3_module_4 (
    .out_5(add_3_module_4_out_5), .out_6(add_3_module_4_out_6), .out_7(add_3_module_4_out_7),
    .out_8(add_3_module_4_out_8), .in_1(add_3_module_5_out_6), .in_2(add_3_module_5_out_7),
    .in_3(add_3_module_5_out_8), .in_4(in_1[3]));
  Add_3_Module add_3_module_5 (
    .out_5(add_3_module_5_out_5), .out_6(add_3_module_5_out_6), .out_7(add_3_module_5_out_7),
    .out_8(add_3_module_5_out_8), .in_1(add_3_module_6_out_6), .in_2(add_3_module_6_out_7),
    .in_3(add_3_module_6_out_8), .in_4(in_1[4]));
  Add_3_Module add_3_module_6 (
    .out_5(add_3_module_6_out_5), .out_6(add_3_module_6_out_6), .out_7(add_3_module_6_out_7),
    .out_8(add_3_module_6_out_8), .in_1(1'b0), .in_2(in_1[7]), .in_3(in_1[6]), .in_4(in_1[5]));
  Add_3_Module add_3_module_7 (
    .out_5(out_2[0]), .out_6(out_3[3]), .out_7(out_3[2]), .out_8(out_3[1]), .in_1(add_3_module_3_out_6),
    .in_2(add_3_module_3_out_7), .in_3(add_3_module_3_out_8), .in_4(in_1[1]));

  assign out_3[0] = in_1[0];
endmodule

// DD
module Display_Driver (
  input  [7:0] data,
  input  [3:0] pos,
  input  [3:0] addr,
  input  clk,
  input  dir,
  output [3:0] out_6,
  output [3:0] out_7,
  output isEmpty,
  output [7:0] register,
  output [7:0] data_2,
  output [3:0] pos_2,
  output [3:0] addr_2,
  output clk_2,
  output dir_2,
  output [3:0] pos_3
);

  wire and_1_out, and_2_out, comparator_1_eq, not_1_out, or_1_out;

  or or_1 (or_1_out, register[7], register[6], register[5], register[4], register[3], register[2], register[1], register[0]);
  assign isEmpty = or_1_out ? 1'b1 : 1'bz;  // Controlled_Buffer controlled_buffer_1
  Comparator #(.width(4)) comparator_1 (.a(addr), .b(pos), .eq(comparator_1_eq));  // open: gt, lt
  and and_1 (and_1_out, comparator_1_eq, dir);
  Register register_1 (.D(data), .en(and_1_out), .Q(register), .clk(clk));  // open: clr
  // Probe on register
  BCD_Converter bcd_converter_1 (.out_2(out_6), .out_3(out_7), .in_1(register));
  assign data_2 = and_2_out ? register : 8'bz;  // Controlled_Buffer controlled_buffer_2
  and and_2 (and_2_out, ~dir, comparator_1_eq);  // AND_Gate
  not not_1 (not_1_out, and_2_out);
  assign data_2 = not_1_out ? data : 8'bz;  // Controlled_Buffer controlled_buffer_3
  Adder #(.width(4)) adder_1 (.a(pos), .b(4'b0001), .out(pos_2));  // open: cin, cout

  assign addr_2 = addr;
  assign clk_2 = clk;
  assign dir_2 = dir;
  assign pos_3 = pos;

  // Notes on the sheet:
  //   Add bcd here
endmodule
